# Fritzing sketch electronics (saved by Fritzing 0.9.3b)

parts:
  Part1 = Arduino Due (Rev2b)
  Part2 = Photon

nets:
  N1: Part1.D16/TX2, Part2.RX
  N2: Part1.D17/RX2, Part2.TX
  GND: Part1.GND, Part2.GND
  VIN: Part1.VIN, Part2.VIN
